# Fritzing sketch BoxenManager (saved by Fritzing 0.9.4)
breadboards: 1

parts:
  Garage_1 = NKK M2032SS1W01 3PDT Toggle Switch [package=THT]
  Garage_2 = NKK M2032SS1W01 3PDT Toggle Switch [package=THT]
  Garage_3 = NKK M2032SS1W01 3PDT Toggle Switch [package=THT]
  Garage_4 = NKK M2032SS1W01 3PDT Toggle Switch [package=THT]
  Garage_5 = NKK M2032SS1W01 3PDT Toggle Switch [package=THT]
  Garage_6 = NKK M2032SS1W01 3PDT Toggle Switch [part_number=" TRU Components Schiebeschalter EAN: 4016139210469" package=THT]
  J1 = shrouded pin header, 16 pins [form="♂ (shrouded male)"]  # not connected
  J2 = shrouded pin header, 16 pins [form="♂ (shrouded male)"]
  LED1 = RGB LED (com. cathode, rgb) [package="5 mm [THT]"]
  LED3 = RGB LED (com. cathode, rgb) [package="5 mm [THT]"]
  LED4 = RGB LED (com. cathode, rgb) [package="5 mm [THT]"]
  LED6 = RGB LED (com. cathode, rgb) [package="5 mm [THT]"]
  LED5 = RGB LED (com. cathode, rgb) [package="5 mm [THT]"]
  LED2 = RGB LED (com. cathode, rgb) [package="5 mm [THT]"]
  R1 = Resistor [tolerance=±5% resistance=47k package=THT]
  R2 = Resistor [tolerance=±5% resistance=47k package=THT]
  R3 = Resistor [tolerance=±5% resistance=47k package=THT]
  R4 = Resistor [tolerance=±5% resistance=47k package=THT]
  8-fach_OR/NOR_Gatter = IC, DIP package, 14 pins [chip_label=HCF4078]
  PullDown_mit_jeweils = Resistor [tolerance=±5% resistance=22k package=THT]
  R6 = Resistor [tolerance=±5% resistance=22k package=THT]
  R7 = Resistor [tolerance=±5% resistance=22k package=THT]
  R8 = Resistor [tolerance=±5% resistance=22k package=THT]
  R9 = Resistor [tolerance=±5% resistance=22k package=THT]
  R10 = Resistor [tolerance=±5% resistance=22k package=THT]
  R11 = Resistor [tolerance=±5% resistance=22k package=THT]
  R12 = Resistor [tolerance=±5% resistance=22k package=THT]
  R13 = Resistor [tolerance=±5% resistance=47k package=THT]
  R14 = Resistor [tolerance=±5% resistance=47k package=THT]
  R15 = Resistor [tolerance=±5% resistance=47k package=THT]
  R16 = Resistor [tolerance=±5% resistance=47k package=THT]
  R17 = Resistor [tolerance=±5% resistance=47k package=THT]
  R18 = Resistor [tolerance=±5% resistance=47k package=THT]
  R19 = Resistor [tolerance=±5% resistance=47k package=THT]
  R20 = Resistor [tolerance=±5% resistance=47k package=THT]

nets:
  14.8V: Garage_1.C1, Garage_1.C2, Garage_2.C1, Garage_2.C2, Garage_3.C1, Garage_3.C2, Garage_4.C1, Garage_4.C2, Garage_5.C1, Garage_5.C2, Garage_6.C1, Garage_6.C2, J2.pin1, 8-fach_OR/NOR_Gatter.pin14
  N1: Garage_1.L1-1, Garage_1.L1-3, J2.pin2, 8-fach_OR/NOR_Gatter.pin2, PullDown_mit_jeweils.Pin_1
  N2: Garage_1.L2-1, R1.Pin_1
  N3: Garage_1.L2-3, J2.pin3, R2.Pin_1
  N4: Garage_2.L1-1, Garage_2.L1-3, J2.pin4, 8-fach_OR/NOR_Gatter.pin3, R7.Pin_1
  N5: Garage_2.L2-1, R3.Pin_1
  N6: Garage_2.L2-3, J2.pin5, R4.Pin_1
  N7: Garage_3.L1-1, Garage_3.L1-3, J2.pin6, 8-fach_OR/NOR_Gatter.pin4, R10.Pin_1
  N8: Garage_3.L2-1, R13.Pin_1
  N9: Garage_3.L2-3, J2.pin7, R14.Pin_1
  N10: Garage_4.L1-1, Garage_4.L1-3, J2.pin8, 8-fach_OR/NOR_Gatter.pin10, R11.Pin_0
  N11: Garage_4.L2-1, R15.Pin_1
  N12: Garage_4.L2-3, J2.pin9, R16.Pin_1
  N13: Garage_5.L1-1, Garage_5.L1-3, J2.pin10, 8-fach_OR/NOR_Gatter.pin11, R9.Pin_0
  N14: Garage_5.L2-1, R17.Pin_1
  N15: Garage_5.L2-3, J2.pin11, R18.Pin_1
  N16: Garage_6.L1-1, Garage_6.L1-3, J2.pin12, 8-fach_OR/NOR_Gatter.pin12, R8.Pin_0
  N17: Garage_6.L2-1, R19.Pin_1
  N18: Garage_6.L2-3, J2.pin13, R20.Pin_1
  N19: J2.pin14, 8-fach_OR/NOR_Gatter.pin13
  N20: J2.pin15, 8-fach_OR/NOR_Gatter.pin1
  GND: J2.pin16, LED1.common_cathode, LED3.common_cathode, LED4.common_cathode, LED6.common_cathode, LED5.common_cathode, LED2.common_cathode, 8-fach_OR/NOR_Gatter.pin7, PullDown_mit_jeweils.Pin_0, R6.Pin_0, R7.Pin_0, R8.Pin_1, R9.Pin_1, R10.Pin_0, R11.Pin_1, R12.Pin_1
  N21: LED1.green_anode, R1.Pin_0
  N22: LED1.blue_anode, R2.Pin_0
  N23: LED3.green_anode, R13.Pin_0
  N24: LED3.blue_anode, R14.Pin_0
  N25: LED4.green_anode, R15.Pin_0
  N26: LED4.blue_anode, R16.Pin_0
  N27: LED6.green_anode, R19.Pin_0
  N28: LED6.blue_anode, R20.Pin_0
  N29: LED5.green_anode, R17.Pin_0
  N30: LED5.blue_anode, R18.Pin_0
  N31: LED2.green_anode, R3.Pin_0
  N32: LED2.blue_anode, R4.Pin_0
  N33: 8-fach_OR/NOR_Gatter.pin5, R6.Pin_1
  N34: 8-fach_OR/NOR_Gatter.pin9, R12.Pin_0

custom parts:
  NKK M2032SS1W01 3PDT Toggle Switch: NKK M2032SS1W01 3PDT Toggle Switch This switch has three poles and two position (Jan 2022 replace pads in pcb with pads with holes)
